# Fritzing sketch myfrigo (saved by Fritzing 0.9.6b)
breadboards: 1

parts:
  Raspberry_Pi_1 = Raspberry Pi 3 [part_number=RPI-3-V1.2]
  dfds = Keyes Relay [package=THT]
  KY-2 = Keyes Relay [package=THT]
  KY-3 = Keyes Relay [package=THT]
  M1 = DC Motor
  M2 = DC Motor
  HLK-PM1 = HLK-PM01
  J1 = female pin header, 2 pins [form="♀ (female)"]
  J2 = female pin header, 2 pins [form="♀ (female)"]
  J3 = female pin header, 2 pins [form="♀ (female)"]
  Power_plug1 = Power plug
  dfds1 = Keyes Relay [package=THT]
  DS1 = DS18B20 1-Wire Temperature Sensor [part_number="DS18B20 Temp sensor"]
  R1 = Resistor [tolerance=±5% resistance=10k package="2512 [SMD]"]
  F1 = Fan - Ventilador [package=THT]
  HLK-PM2 = HLK-PM01
  J5 = female pin header, 2 pins [form="♀ (female)"]
  J6 = female pin header, 2 pins [form="♀ (female)"]
  HLK-PM3 = HLK-PM01
  J7 = female pin header, 2 pins [form="♀ (female)"]

nets:
  5V: Raspberry_Pi_1.GPIO2, Raspberry_Pi_1.GPIO3, Raspberry_Pi_1.5V, dfds.NO, dfds1.power, DS1.VDD
  N1: Raspberry_Pi_1.GIPO4, DS1.DQ, R1.Pin_0
  GND: Raspberry_Pi_1.GND, Raspberry_Pi_1.GIPO14, dfds.C, dfds1.ground, DS1.GND
  N2: Raspberry_Pi_1.GIPO23, dfds1.signal
  N3: dfds.signal, dfds.power, J1.pin1
  N4: dfds.ground, HLK-PM1.-Vo
  N5: KY-2.C, KY-3.C, J5.pin1
  N6: KY-2.NO, M2.pin_1, J3.pin2
  N7: KY-3.NO, M1.pin_1
  N8: M1.pin_2, M2.pin_2, J2.pin2, J6.pin1
  N9: HLK-PM1.AC#0, J3.pin1, dfds1.NO
  N10: HLK-PM1.AC#1, J2.pin1, dfds1.C
  N11: HLK-PM1.+Vo, J1.pin2
  N12: Power_plug1.GND, HLK-PM2.AC#1, J6.pin2, HLK-PM3.AC#1
  N13: Power_plug1.VCC, HLK-PM2.AC#0, J5.pin2, HLK-PM3.AC#0
  N14: F1.5V, HLK-PM2.-Vo
  N15: F1.GND, HLK-PM2.+Vo
  N16: HLK-PM3.-Vo, J7.pin1
  N17: HLK-PM3.+Vo, J7.pin2

notes:
  Fridge compressor
  mother board
  - the motherboard commands the 2 compressor relays
  Relay monitoring compressor
  220V
  blue : neutral, common
  brown : active phase
  Freezer compressor
  convert 220 to 5v when compressor is ON (still a GSM charger)<module fritzingVersion="0.9.6b.2021-02-21.CD-175-0-8a1e0682">
  <boundingRects>
  <boundingRect name="Schematic View" rect="-702.054 45.2112 138.6 90"/>
  <boundingRect name="Breadboard View" rect="102.432 -215.746 120.472 71.5748"/>
  <boundingRect name="PCB View" rect="918.816 9.38707 120.472 71.5748"/>
  </boundingRects>
  <instances>
  <instance moduleIdRef="HLK-PM01_f3fff412ac55f21b5b3168355aacbaa9_1" path="D:/Program Files/Fritzing/fritzing-parts/core/HLK-PM01.fzp" modelIndex="85411657">
  <title>HLK-PM1</title>
  <views>
  <breadboardView layer="breadboard">
  <geometry x="102.432" z="2.50052" y="-215.746">
  <transform m11="-1" m22="-1" m13="0" m21="0" m31="120.472" m12="0" m23="0" m32="71.5748" m33="1"/>
  </geometry>
  <titleGeometry x="615.328" xOffset="512.896" yOffset="-825.572" textColor="#000000" y="-1041.32" z="5.00042" visible="true" fontSize="9">
  <displayKey key=""/>
  <displayKey key="part number"/>
  </titleGeometry>
  <connectors>
  <connector layer="breadboard" connectorId="connector0">
  <geometry x="0" y="0"/>
  <connects/>
  </connector>
  <connector layer="breadboard" connectorId="connector2">
  <geometry x="0" y="0"/>
  <connects/>
  </connector>
  <connector layer="breadboard" connectorId="connector1">
  <geometry x="0" y="0"/>
  <connects/>
  </connector>
  <connector layer="breadboard" connectorId="connector3">
  <geometry x="0" y="0"/>
  <connects/>
  </connector>
  </connectors>
  </breadboardView>
  <pcbView layer="copper0">
  <geometry x="918.816" z="5.50045" y="9.38707"/>
  <titleGeometry x="1039.29" xOffset="120.472" yOffset="-7" textColor="#000000" y="2.38707" z="13.0001" visible="true" fontSize="5">
  <displayKey key=""/>
  </titleGeometry>
  <connectors>
  <connector layer="copper0" connectorId="connector0">
  <geometry x="0" y="0"/>
  <connects/>
  </connector>
  <connector layer="copper0" connectorId="connector2">
  <geometry x="0" y="0"/>
  <connects/>
  </connector>
  <connector layer="copper0" connectorId="connector1">
  <geometry x="0" y="0"/>
  <connects/>
  </connector>
  <connector layer="copper0" connectorId="connector3">
  <geometry x="0" y="0"/>
  <connects/>
  </connector>
  </connectors>
  </pcbView>
  <schematicView layer="schematic">
  <geometry x="-702.054" z="2.50045" y="45.2112"/>
  <titleGeometry x="-563.454" xOffset="138.6" yOffset="-7" textColor="#000000" y="38.2112" z="7.00007" visible="true" fontSize="5">
  <displayKey key=""/>
  <displayKey key="part number"/>
  </titleGeometry>
  <connectors>
  <connector layer="schematic" connectorId="connector0">
  <geometry x="0" y="0"/>
  <connects/>
  </connector>
  <connector layer="schematic" connectorId="connector2">
  <geometry x="0" y="0"/>
  <connects/>
  </connector>
  <connector layer="schematic" connectorId="connector1">
  <geometry x="0" y="0"/>
  <connects/>
  </connector>
  <connector layer="schematic" connectorId="connector3">
  <geometry x="0" y="0"/>
  <connects/>
  </connector>
  </connectors>
  </schematicView>
  </views>
  </instance>
  </instances>
  </module>
  Relay commanding compressor
  DS18B20 Temp Sensor (cable)
  convert 220 to 9v for fan ON (still an old converter)
  DS18B20 Temp Sensor
  Blue : Ground
  Red : 5V
  Yellow : Data (GPIO4)

custom parts:
  Keyes Relay: The Keyes 5V relay module is suitable for SCM development, home appliance control. It uses a 5V~12V TIL control signal which can control DC / AC signal.
  Fan - Ventilador: Ventilador de 2 pines, se encuentra comunmente en computadoras de escritorio
