# Fritzing sketch zfrigo-raspberry (saved by Fritzing 0.9.6b)
breadboards: 1

parts:
  Raspberry_Pi_1 = Raspberry Pi 3 [part_number=RPI-3-V1.2]
  dfds = Keyes Relay [package=THT]
  KY-2 = Keyes Relay [package=THT]
  KY-3 = Keyes Relay [package=THT]
  M1 = DC Motor
  M2 = DC Motor
  HLK-PM1 = HLK-PM01
  J1 = female pin header, 2 pins [form="♀ (female)"]
  J2 = female pin header, 2 pins [form="♀ (female)"]
  J3 = female pin header, 2 pins [form="♀ (female)"]
  Power_plug1 = Power plug
  dfds1 = Keyes Relay [package=THT]
  DS1 = DS18B20 1-Wire Temperature Sensor [part_number="DS18B20 Temp sensor"]
  R1 = Resistor [tolerance=±5% resistance=10k package="2512 [SMD]"]
  F1 = Fan - Ventilador [package=THT]
  HLK-PM2 = HLK-PM01
  J5 = female pin header, 2 pins [form="♀ (female)"]
  J6 = female pin header, 2 pins [form="♀ (female)"]
  HLK-PM3 = HLK-PM01
  J7 = female pin header, 2 pins [form="♀ (female)"]

nets:
  5V: Raspberry_Pi_1.GPIO2, Raspberry_Pi_1.GPIO3, Raspberry_Pi_1.5V, dfds.NO, dfds1.power, DS1.VDD
  N1: Raspberry_Pi_1.GIPO4, DS1.DQ, R1.Pin_0
  GND: Raspberry_Pi_1.GND, Raspberry_Pi_1.GIPO14, dfds.C, dfds1.ground, DS1.GND
  N2: Raspberry_Pi_1.GIPO23, dfds1.signal
  N3: dfds.signal, dfds.power, J1.pin1
  N4: dfds.ground, HLK-PM1.-Vo
  N5: KY-2.C, KY-3.C, J5.pin1
  N6: KY-2.NO, M2.pin_1, J3.pin2
  N7: KY-3.NO, M1.pin_1
  N8: M1.pin_2, M2.pin_2, J2.pin2, J6.pin1
  N9: HLK-PM1.AC#0, J3.pin1, dfds1.NO
  N10: HLK-PM1.AC#1, J2.pin1, dfds1.C
  N11: HLK-PM1.+Vo, J1.pin2
  N12: Power_plug1.GND, HLK-PM2.AC#1, J6.pin2, HLK-PM3.AC#1
  N13: Power_plug1.VCC, HLK-PM2.AC#0, J5.pin2, HLK-PM3.AC#0
  N14: F1.5V, HLK-PM2.-Vo
  N15: F1.GND, HLK-PM2.+Vo
  N16: HLK-PM3.-Vo, J7.pin1
  N17: HLK-PM3.+Vo, J7.pin2

notes:
  Fridge compressor
  mother board
  - the motherboard commands the 2 compressor relays
  Relay monitoring compressor
  220V
  blue : neutral, common
  brown : active phase
  Freezer compressor
  Relay commanding compressor
  Blue : Ground
  Orange : +5V White : GPIO23 (16)
  DS18B20 Temp Sensor (cable)
  convert 220 to 9v for fan ON (still an old converter)
  DS18B20 Temp Sensor
  Blue : Ground
  Red : +5V
  Yellow : Data (GPIO4) (7)
  convert 220 to 5v when compressor is ON
  élément chauffant freezer

custom parts:
  Keyes Relay: The Keyes 5V relay module is suitable for SCM development, home appliance control. It uses a 5V~12V TIL control signal which can control DC / AC signal.
  Fan - Ventilador: Ventilador de 2 pines, se encuentra comunmente en computadoras de escritorio
